// Digital circuit part_c.dig as structural Verilog
module part_c (
  input  in_0,
  input  in_1,
  input  in_2,
  output out_0
);

  wire nmos_s, pmos_2_d, pmos_4_d, pmos_5_d, pmos_6_d, pmos_d;

  PFET \pmos  (.G(in_0), .S(1'b1), .D(pmos_d));
  NFET \nmos  (.G(in_0), .D(pmos_d), .S(nmos_s));
  NFET nmos_2 (.G(in_1), .D(nmos_s), .S(1'b0));
  PFET pmos_2 (.G(in_2), .S(1'b1), .D(pmos_2_d));
  FGNFET nmos_3 (.G(in_2), .D(pmos_2_d), .S(1'b0));
  PFET pmos_3 (.G(in_1), .S(1'b1), .D(pmos_d));
  PFET pmos_4 (.G(pmos_d), .S(1'b1), .D(pmos_4_d));
  FGNFET nmos_4 (.G(pmos_d), .D(pmos_4_d), .S(1'b0));
  PFET pmos_5 (.G(pmos_4_d), .S(1'b1), .D(pmos_5_d));
  PFET pmos_6 (.G(pmos_2_d), .S(pmos_5_d), .D(pmos_6_d));
  NFET #(.unidirectional("true")) nmos_5 (.G(pmos_2_d), .D(pmos_6_d), .S(1'b0));
  NFET nmos_6 (.G(pmos_4_d), .D(pmos_6_d), .S(1'b0));
  PFET pmos_7 (.G(pmos_6_d), .S(1'b1), .D(out_0));
  FGNFET nmos_7 (.G(pmos_6_d), .D(out_0), .S(1'b0));
endmodule

/* Test case part_c_test:
in_0 in_1 in_2 out_0
0 0 0 1
0 0 1 0
0 1 0 1
0 1 1 0
1 0 0 1
1 0 1 0 
1 1 0 1 
1 1 1 1
*/
