// Digital circuit lab2_part1.dig as structural Verilog
module lab2_part1 (
  input  inA_0,
  input  inA_1,
  input  inA_2,
  input  inA_3,
  input  inB_0,
  input  inB_1,
  input  inB_2,
  input  inB_3,
  output out0,
  output out1,
  output out2,
  output out3
);

  wire int0, int1, int2, int3;

  Multiplexer multiplexer_1 (.sel(inB_0), .in_0(inA_3), .in_1(inA_0), .out(int3));
  Multiplexer multiplexer_2 (.sel(inB_1), .in_0(int3), .in_1(int1), .out(out3));
  Multiplexer multiplexer_3 (.sel(inB_0), .in_0(inA_2), .in_1(inA_3), .out(int2));
  Multiplexer multiplexer_4 (.sel(inB_1), .in_0(int2), .in_1(int0), .out(out2));
  Multiplexer multiplexer_5 (.sel(inB_0), .in_0(inA_1), .in_1(inA_2), .out(int1));
  Multiplexer multiplexer_6 (.sel(inB_1), .in_0(int1), .in_1(int3), .out(out1));
  Multiplexer multiplexer_7 (.sel(inB_0), .in_0(inA_0), .in_1(inA_1), .out(int0));
  Multiplexer multiplexer_8 (.sel(inB_1), .in_0(int0), .in_1(int2), .out(out0));

  // Notes on the sheet:
  //   Interface (do not edit the content inside this box)
  //   Inputs
  //   Outputs
  //   Rotatee:
  //   Rotation amount:
  //   Result of Rotating  input A by the amount given by input B:
endmodule

/* Test case:
inA_3 inA_2 inA_1 inA_0 inB_1 inB_0  out3 out2 out1 out0
 0     0     0     0     0     0      0    0    0    0  
 0     0     0     1     0     0      0    0    0    1  
 0     0     0     1     0     1      1    0    0    0  
 0     0     0     1     1     0      0    1    0    0  
 0     0     0     1     1     1      0    0    1    0   
 0     1     0     1     0     0      0    1    0    1  
 0     1     0     1     0     1      1    0    1    0  
 0     1     0     1     1     0      0    1    0    1  
 0     1     0     1     1     1      1    0    1    0  
*/
