// Digital circuit lab2_part2.dig as structural Verilog
module lab2_part2 (
  input  in0,
  input  in1,
  input  in2,
  input  in3,
  output seg_a,
  output seg_f,
  output seg_b,
  output seg_g,
  output seg_e,
  output seg_c,
  output seg_d,
  output seg_dp,
  output sign_a,
  output sign_f,
  output sign_b,
  output sign_g,
  output sign_e,
  output sign_c,
  output sign_d,
  output sign_dp
);

  wire A, add_1_c_o, add_2_c_o, add_3_c_o, B, C, carry, D, multiplexer_3_out, newin0, newin1, newin2, newin3,
       not_1_out, not_2_out, not_3_out, not_4_out, not_5_out, not_6_out, not_7_out, not_8_out, not_9_out,
       not_10_out, not_11_out, not_12_out, not_13_out, not_14_out, not_15_out, not_16_out, not_17_out,
       not_18_out, not_19_out, not_20_out, not_21_out, not_22_out, not_23_out, not_24_out, not_25_out,
       not_26_out, not_27_out;

  Multiplexer multiplexer_1 (.sel(in3), .in_0(1'b0), .in_1(1'b1), .out(sign_g));
  Multiplexer multiplexer_2 (.sel(sign_g), .in_0(in3), .in_1(not_1_out), .out(newin3));
  not not_1 (not_1_out, in3);
  Multiplexer multiplexer_3 (.sel(sign_g), .in_0(1'b0), .in_1(1'b1), .out(multiplexer_3_out));
  Add add_1 (.a(newin0), .b(multiplexer_3_out), .c_i(1'b0), .s(D), .c_o(add_1_c_o));
  not not_2 (not_2_out, A);
  not not_3 (not_3_out, B);
  not not_4 (not_4_out, C);
  not not_5 (not_5_out, D);
  not not_6 (not_6_out, A);
  not not_7 (not_7_out, B);
  not not_8 (not_8_out, C);
  not not_9 (not_9_out, A);
  not not_10 (not_10_out, B);
  not not_11 (not_11_out, D);
  not not_12 (not_12_out, A);
  not not_13 (not_13_out, B);
  not not_14 (not_14_out, A);
  not not_15 (not_15_out, C);
  not not_16 (not_16_out, D);
  not not_17 (not_17_out, A);
  not not_18 (not_18_out, C);
  not not_19 (not_19_out, A);
  not not_20 (not_20_out, D);
  not not_21 (not_21_out, A);
  not not_22 (not_22_out, B);
  not not_23 (not_23_out, C);
  not not_24 (not_24_out, D);
  not not_25 (not_25_out, in2);
  Multiplexer multiplexer_4 (.sel(sign_g), .in_0(in2), .in_1(not_25_out), .out(newin2));
  and and_1 (seg_a, not_2_out, not_3_out, not_4_out, not_5_out);
  and and_2 (seg_a, not_6_out, not_7_out, not_8_out, D);
  and and_3 (seg_a, not_9_out, not_10_out, C, not_11_out);
  and and_4 (seg_a, not_12_out, not_13_out, C, D);
  and and_5 (seg_a, not_14_out, B, not_15_out, not_16_out);
  and and_6 (seg_a, not_17_out, B, not_18_out, D);
  and and_7 (seg_a, not_19_out, B, C, not_20_out);
  and and_8 (seg_a, not_21_out, B, C, D);
  and and_9 (seg_a, A, not_22_out, not_23_out, not_24_out);
  Add add_2 (.a(newin1), .b(add_1_c_o), .c_i(1'b0), .s(C), .c_o(add_2_c_o));
  not not_26 (not_26_out, in1);
  Seven_Seg seven_seg_1 (.a(1'b0), .b(1'b0), .c(1'b0), .d(1'b0), .e(1'b0), .f(1'b0), .g(sign_g), .dp(1'b0));
  Multiplexer multiplexer_5 (.sel(sign_g), .in_0(in1), .in_1(not_26_out), .out(newin1));
  Add add_3 (.a(newin2), .b(add_2_c_o), .c_i(1'b0), .s(B), .c_o(add_3_c_o));
  Seven_Seg seven_seg_2 (.a(seg_a), .b(seg_a), .c(seg_a), .d(seg_a), .e(seg_a), .f(seg_a), .g(seg_a), .dp(1'b0));
  not not_27 (not_27_out, in0);
  Multiplexer multiplexer_6 (.sel(sign_g), .in_0(in0), .in_1(not_27_out), .out(newin0));
  Add add_4 (.a(newin3), .b(add_3_c_o), .c_i(1'b0), .s(A), .c_o(carry));

  assign seg_b = seg_a;
  assign seg_c = seg_a;
  assign seg_d = seg_a;
  assign seg_dp = 1'b0;
  assign seg_e = seg_a;
  assign seg_f = seg_a;
  assign seg_g = seg_a;
  assign sign_a = 1'b0;
  assign sign_b = 1'b0;
  assign sign_c = 1'b0;
  assign sign_d = 1'b0;
  assign sign_dp = 1'b0;
  assign sign_e = 1'b0;
  assign sign_f = 1'b0;

  // Notes on the sheet:
  //   Sign Generator
  //   Neg --> Pos
  //   Add One
  //   Hardwiring each number
  //   0
  //   1
  //   2
  //   3
  //   4
  //   5
  //   6
  //   7
  //   8
  //   Interface (do not edit the content inside this box)
  //   Outputs:
  //   Inputs
  //   Sign
  //   Decimal Number
endmodule

/* Test case:
in3 in2 in1 in0  sign_a sign_b sign_c sign_d sign_e sign_f sign_g  seg_a seg_b seg_c seg_d seg_e seg_f seg_g
 0   0   0   0    0      0      0      0      0      0      0       1     1     1     1     1     1     0
*/
